# Fritzing sketch PlantSystem Full Fritz (saved by Fritzing 0.9.4)
breadboards: 1

parts:
  Argon1 = Particle Argon
  OLED_I2C1 = OLED 128x64 I2C Monochrome Display
  M1 = BMP280
  R1 = Resistor [tolerance=±5% resistance=2.2k package="0805 [SMD]"]
  R2 = Resistor [tolerance=±5% resistance=220 package="0805 [SMD]"]
  Q1 = PNP-Transistor [package="TO92 [THT]"]
  Relay1 = Relay - 6 pins [package="DIP (Dual Inline) [THT]"]
  M2 = DC Motor
  SENS1 = SoilWatch 10
  Grove1 = Grove Dust Sensor
  Part1 = MQ-131 breakout

nets:
  VCC: Argon1.3.3V, OLED_I2C1.VDD, M1.VIN, SENS1.VCC, Part1.VCC
  GND: Argon1.GND, OLED_I2C1.GND, M1.GND, R1.Pin_1, Q1.E, Relay1.GND, M2.pin_2, SENS1.GND, Grove1.GND, Part1.GND
  N1: Argon1.A0, SENS1.OUT
  N2: Argon1.A1, Grove1.SIG
  N3: Argon1.A2, Part1.DO
  N4: Argon1.SDA, OLED_I2C1.SDA, M1.SDA
  N5: Argon1.SCL, OLED_I2C1.SCK, M1.SCL
  N6: Argon1.D7, R1.Pin_0, Q1.B
  VCC_2: Argon1.VUSB, R2.Pin_1, Relay1.VCC, Relay1.ON, Grove1.VCC
  N7: R2.Pin_0, Q1.C, Relay1.IN
  N8: Relay1.COM, M2.pin_1

custom parts:
  Particle Argon: The Argon is a powerful Wi-Fi enabled development board that can act as either a standalone Wi-Fi endpoint or Wi-Fi enabled gateway for Particle Mesh networks. It is based on the Nordic nRF52840 and has built-in battery charging circuitry so it’s easy to connect a Li-Po and deploy your local network in minutes. The Argon is great for connecting existing projects to the Particle Device Cloud or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
  BMP280: Temperature Humidity Barometric presure Sensor, I2C
  Relay - 6 pins: A DIP stand-in part for whatever IC you want. With 6 pins on a 900mil dual inline package (DIP) footprint.
  SoilWatch 10: SoilWatch 10 - Capacitive soil moisture sensor
  Grove Dust Sensor: PPD42 Grove Dust Sensor
  MQ-131 breakout: SKU: 101282
